# Fritzing sketch RPi LCD Verbindung V2 - final (saved by Fritzing 0.9.2b)
stripboards: 1

parts:
  U1 = LCD-16X2 [package=lcd-16x2_noholes]
  S1 = Pushbutton [package="[THT]"]
  LED1 = LED - 5mm [color="Red (633nm)" package="5 mm [THT]"]
  R4 = Trimmer Potentiometer [maximum_resistance=10kΩ package=THT]  # not connected
  R5 = Resistor [tolerance=±5% resistance=220 package="0805 [SMD]"]
  C1 = Ceramic Capacitor [capacitance=100nF package="100 mil [THT, multilayer]"]
  Raspberry_Pi1 = Raspberry Pi 2
  R3 = Trimmer Potentiometer [maximum_resistance=10kΩ package=THT]  # not connected
  U2 = Voltage Regulator - 5V [package="TO220 [THT]"]

nets:
  GND: U1.VSS, U1.R_W, U1.K, LED1.cathode, Raspberry_Pi1.GND, U2.GND
  N1: S1.Pin_1, S1.Pin_2, R5.Pin_0
  N2: S1.Pin_3, S1.Pin_4
  N3: C1.1, U2.input_voltage
